# Fritzing sketch h_bridge (saved by Fritzing 0.9.4)
breadboards: 1

parts:
  Q2 = Basic FET P-Channel [package="TO220 [THT]"]
  Q1 = Basic FET P-Channel [package="TO220 [THT]"]
  Q4 = Basic FET N-Channel [package="TO220 [THT]"]
  Q3 = Basic FET N-Channel [package="TO220 [THT]"]
  Part1 = Pololu 3.3V Step-Up Voltage Regulator U1V11F3
  R1 = Resistor [tolerance=±5% resistance=100 package=THT]
  R2 = Resistor [tolerance=±5% resistance=100 package=THT]
  R3 = Resistor [tolerance=±5% resistance=5k package=THT]
  R4 = Resistor [tolerance=±5% resistance=5k package=THT]

nets:
  N1: Q2.gate, Q4.gate, R2.Pin_1, R3.Pin_0
  N2: Q2.drain, Q1.drain
  N3: Q2.source, Q4.drain, Part1.IN1
  N4: Q1.gate, Q3.gate, R1.Pin_1, R4.Pin_0
  N5: Q1.source, Q3.drain, Part1.IN2
  N6: Q4.source, Q3.source, R3.Pin_1, R4.Pin_1

notes:
  G, D, S
  VCC
  GND
