# Fritzing sketch micromouse (saved by Fritzing 0.9.4)
breadboards: 2

parts:
  Q5 = Basic FET N-Channel [package="TO220 [THT]"]
  Q6 = Basic FET P-Channel [package="TO220 [THT]"]
  Q7 = Basic FET N-Channel [package="TO220 [THT]"]
  Q8 = Basic FET P-Channel [package="TO220 [THT]"]
  Part2 = Pololu 3.3V Step-Up Voltage Regulator U1V11F3
  R5 = Resistor [tolerance=±5% resistance=100 package=THT]
  R6 = Resistor [tolerance=±5% resistance=100 package=THT]
  R7 = Resistor [tolerance=±5% resistance=5k package=THT]
  R8 = Resistor [tolerance=±5% resistance=5k package=THT]
  Q9 = Basic FET N-Channel [package="TO220 [THT]"]
  Q10 = Basic FET P-Channel [package="TO220 [THT]"]
  Q11 = Basic FET N-Channel [package="TO220 [THT]"]
  Q12 = Basic FET P-Channel [package="TO220 [THT]"]
  R9 = Resistor [tolerance=±5% resistance=100 package=THT]
  R10 = Resistor [tolerance=±5% resistance=100 package=THT]
  R11 = Resistor [tolerance=±5% resistance=5k package=THT]
  R12 = Resistor [tolerance=±5% resistance=5k package=THT]
  Part3 = Pololu 3.3V Step-Up Voltage Regulator U1V11F3
  U1 = Magnetic Encoder
  U2 = Magnetic Encoder
  U3 = LuaNode32 / ESP32 [part_number=ESP32S-PIN30]
  Grove1 = Grove OLED 128x96
  S1 = Pushbutton [package="[THT]"]
  R13 = Resistor [tolerance=±5% resistance=220 package=THT]

nets:
  N1: Q5.gate, Q6.gate, R5.Pin_1, R8.Pin_0
  N2: Q5.drain, Q6.source, Part2.IN1, U1.M1
  N3: Q5.source, Q7.source, R7.Pin_1, R8.Pin_1, Q9.source, Q11.source, R11.Pin_1, R12.Pin_1
  N4: Q6.drain, Q8.drain
  N5: Q7.gate, Q8.gate, R6.Pin_1, R7.Pin_0
  N6: Q7.drain, Q8.source, Part2.IN2, U1.M2
  N7: R5.Pin_0, U3.D12
  N8: R6.Pin_0, U3.D13
  N9: Q9.gate, Q10.gate, R9.Pin_1, R12.Pin_0
  N10: Q9.drain, Q10.source, Part3.IN1, U2.M1
  N11: Q11.gate, Q12.gate, R10.Pin_1, R11.Pin_0
  N12: Q11.drain, Q12.source, Part3.IN2, U2.M2
  N13: R9.Pin_0, U3.D27
  N14: R10.Pin_0, U3.D14
  N15: U1.OUTB, U3.D25
  N16: U1.OUTA, U3.D26
  N17: U2.OUTB, U3.D32
  N18: U2.OUTA, U3.D33
  N19: U3.D21, Grove1.SDA
  N20: U3.D22, Grove1.SCL
  N21: U3.D23, S1.Pin_1, S1.Pin_2, R13.Pin_0
  N22: S1.Pin_3, S1.Pin_4

notes:
  GND
  7.6V +
  G, D, S
  5V +

custom parts:
  Magnetic Encoder: Magnetic Encoder for Micro Metal Gearmotors, 12 CPR, 2.7-18V
  LuaNode32 / ESP32: New Image for LuaNode32 DOIT ESP32 DEVKIT V1. Base parts from LuaNode32 / ESP32 ESP32 based LuaNode32 by G.Noorlander DOIT Esp32 DevKit v1 (30 pins long, 11 pins width) by Werner Rothschopf (modified by vanepp Dec 2018)
